// Logisim project FF_Contador, de 0 a 10.circ as structural Verilog: 1 circuit, main circuit main
module main (
  input  in_1,
  output Q3,
  output Q2,
  output Q1,
  output Q0
);

  wire j_k_ff_1_qn, j_k_ff_3_qn, or_1_out, or_2_out, Q0_Q1_2_out, Q0_Q1_out;

  and Q0_Q1 (Q0_Q1_out, Q0_Q1_2_out, Q2);
  J_K_Flip_Flop j_k_ff_1 (.J(Q0_Q1_out), .clk(in_1), .K(Q1), .Q(Q3), .Qn(j_k_ff_1_qn));  // open: preset, en, reset
  and Q0_Q1_2 (Q0_Q1_2_out, Q1, Q0);
  or or_1 (or_1_out, Q3, Q0);
  J_K_Flip_Flop j_k_ff_2 (.J(Q0_Q1_2_out), .clk(in_1), .K(Q0_Q1_2_out), .Q(Q2));  // open: Qn, preset, en, reset
  J_K_Flip_Flop j_k_ff_3 (.J(Q0), .clk(in_1), .K(or_1_out), .Q(Q1), .Qn(j_k_ff_3_qn));  // open: preset, en, reset
  or or_2 (or_2_out, j_k_ff_3_qn, j_k_ff_1_qn);
  J_K_Flip_Flop j_k_ff_4 (.J(or_2_out), .clk(in_1), .K(1'b1), .Q(Q0));  // open: Qn, preset, en, reset
endmodule
